# Fritzing sketch TitanRGBDiagram (saved by Fritzing 0.9.3b)
breadboards: 1

parts:
  Nano = Arduino Nano (Rev3.0)
  ZS-042_RTC1 = ZS-042 RTC Module
  LED1-Segm1 = ws2812b [package="smd 2812b"]
  LED1-Segm2 = ws2812b [package="smd 2812b"]
  Blink1 = ws2812b [package="smd 2812b"]
  1000 = Electrolytic Capacitor [capacitance=1µF package="100 mil [THT, electrolytic]"]
  Blink2 = ws2812b [package="smd 2812b"]

nets:
  VSS: Nano.GND, ZS-042_RTC1.GND, LED1-Segm1.VSS, LED1-Segm2.VSS, Blink1.VSS, 1000.-, Blink2.VSS
  N1: Nano.D6, Blink1.DIN
  N2: Nano.D9, LED1-Segm1.DIN
  VDD: Nano.5V, ZS-042_RTC1.VCC, LED1-Segm1.VDD, LED1-Segm2.VDD, Blink1.VDD, 1000.+, Blink2.VDD
  N3: Nano.A5, ZS-042_RTC1.SCL
  N4: Nano.A4, ZS-042_RTC1.SDA
  N5: LED1-Segm1.DOUT, LED1-Segm2.DIN
  N6: Blink1.DOUT, Blink2.DIN

notes:
  Repeat led segments
  until you got 7 segment x 4 digits
